# Fritzing sketch mega_pwm_led_driver (saved by Fritzing 0.9.3b)
circuit board: 10.1548cm x 5.34529cm

parts:
  IC1 = ULN2803A [package=THT]
  IC2 = ULN2803A [package=THT]
  J1 = male pin header, 4 pins [form="♂ (male)"]
  J2 = male pin header, 4 pins [form="♂ (male)"]
  J3 = male pin header, 4 pins [form="♂ (male)"]
  J4 = male pin header, 4 pins [form="♂ (male)"]
  J5 = male pin header, 4 pins [form="♂ (male)"]
  Power_plug1 = Power plug
  Power_plug2 = Power plug
  Bauteil1 = Arduino Mega Proto Shield

nets:
  N1: IC1.In_1, Bauteil1.D6, Bauteil1.N$244
  N2: IC1.In_2, Bauteil1.D7, Bauteil1.N$251
  N3: IC1.In_3, Bauteil1.D8, Bauteil1.N$272
  N4: IC1.In_4, Bauteil1.D9, Bauteil1.N$279
  N5: IC1.In_5, Bauteil1.D10, Bauteil1.N$300
  N6: IC1.In_6, Bauteil1.D11, Bauteil1.N$307
  N7: IC1.In_7, Bauteil1.D12, Bauteil1.N$329
  N8: IC1.In_8, Bauteil1.D13, Bauteil1.N$352
  GND: IC1.0V, IC2.0V, Power_plug1.GND, Power_plug2.GND, Bauteil1.GND, Bauteil1.N$216, Bauteil1.N$362, Bauteil1.N$420, Bauteil1.N$431
  N9: IC1.COM_-_Common, Bauteil1.N$365
  N10: IC1.Out_8, Bauteil1.N$349
  N11: IC1.Out_7, Bauteil1.N$332
  N12: IC1.Out_6, Bauteil1.N$310
  N13: IC1.Out_5, Bauteil1.N$297
  N14: IC1.Out_4, Bauteil1.N$282
  N15: IC1.Out_3, Bauteil1.N$269
  N16: IC1.Out_2, Bauteil1.N$254
  N17: IC1.Out_1, Bauteil1.N$241
  N18: IC2.In_1, Bauteil1.N$107
  N19: IC2.In_2, Bauteil1.D28, Bauteil1.N$110
  N20: IC2.In_3, Bauteil1.D30, Bauteil1.N$134
  N21: IC2.In_4, Bauteil1.D45, Bauteil1.N$139
  N22: IC2.In_5, Bauteil1.D2, Bauteil1.N$160
  N23: IC2.In_6, Bauteil1.D3, Bauteil1.N$167
  N24: IC2.In_7, Bauteil1.D4, Bauteil1.N$188
  N25: IC2.In_8, Bauteil1.D5, Bauteil1.N$195
  N26: IC2.COM_-_Common, Bauteil1.N$213
  N27: IC2.Out_8, Bauteil1.N$198
  N28: IC2.Out_7, Bauteil1.N$185
  N29: IC2.Out_6, Bauteil1.N$170
  N30: IC2.Out_5, Bauteil1.N$157
  N31: IC2.Out_4, Bauteil1.N$142
  N32: IC2.Out_3, Bauteil1.N$131
  N33: IC2.Out_2, Bauteil1.N$113
  N34: IC2.Out_1, Bauteil1.N$104
  N35: J1.pin1, Bauteil1.N$378
  N36: J1.pin2, Bauteil1.N$369
  N37: J1.pin3, Bauteil1.N$345
  N38: J1.pin4, Bauteil1.N$336
  N39: J2.pin1, Bauteil1.N$293
  N40: J2.pin2, Bauteil1.N$286
  N41: J2.pin3, Bauteil1.N$265
  N42: J2.pin4, Bauteil1.N$258
  N43: J3.pin1, Bauteil1.N$237
  N44: J3.pin2, Bauteil1.N$230
  N45: J3.pin3, Bauteil1.N$209
  N46: J3.pin4, Bauteil1.N$202
  N47: J4.pin1, Bauteil1.N$174
  N48: J4.pin2, Bauteil1.N$153
  N49: J4.pin3, Bauteil1.N$146
  N50: J4.pin4, Bauteil1.N$124
  N51: J5.pin1, Bauteil1.N$100
  N52: J5.pin2, Bauteil1.N$93
  N53: J5.pin3, Bauteil1.N$76
  N54: J5.pin4, Bauteil1.N$69
  N55: Power_plug1.VCC, Bauteil1.N$419
  N56: Power_plug2.VCC, Bauteil1.N$429
